// Logisim project p3.circ as structural Verilog: 1 circuit, main circuit main
module main (
  input  in_1,
  input  in_2
);

  wire clock_1_out;
  wire [1:0] rom_1_data;
  wire [2:2] rom_1_data_2;
  wire [4:0] rom_1_data_3;
  wire [6:0] R1_q;
  wire [7:0] adder_1_out, adder_2_out, bit_extender_1_out, multiplexer_1_out, multiplexer_2_out,
       multiplexer_3_out, multiplexer_4_out, pc_q, subtractor_1_out, subtractor_2_out;
  wire [7:7] R1_q_2;

  Clock clock_1 (.out(clock_1_out));
  Register pc (.D(adder_1_out), .en(1'b1), .clk(clock_1_out), .Q(pc_q), .clr(in_2));
  ROM rom_1 (.addr(pc_q), .data({rom_1_data_3, rom_1_data_2[2], rom_1_data}));
  Adder adder_1 (.a(pc_q), .b({8{1'b0}}), .out(adder_1_out), .cin(1'b1));  // open: cout
  assign bit_extender_1_out = {{2{rom_1_data_3[4]}}, {rom_1_data_3, rom_1_data_2[2]}};  // Bit_Extender bit_extender_1
  Register R1 (.D(multiplexer_4_out), .en(1'b1), .clk(clock_1_out), .Q({R1_q_2[7], R1_q}), .clr(in_1));
  Multiplexer #(.width(8)) multiplexer_1 (
    .in0({R1_q_2[7], R1_q}), .in1(subtractor_1_out), .out(multiplexer_1_out), .sel(R1_q_2[7]));
  Subtractor subtractor_1 (.a({8{1'b0}}), .b({R1_q_2[7], R1_q}), .out(subtractor_1_out));  // open: bin, bout
  Multiplexer #(.width(8)) multiplexer_2 (
    .in0({R1_q_2[7], R1_q}), .in1(8'ha), .out(multiplexer_2_out), .sel(R1_q_2[7]));
  Adder adder_2 (.a({R1_q_2[7], R1_q}), .b(bit_extender_1_out), .out(adder_2_out));  // open: cin, cout
  Subtractor subtractor_2 (.a({R1_q_2[7], R1_q}), .b(bit_extender_1_out), .out(subtractor_2_out));  // open: bin, bout
  Multiplexer #(.width(8)) multiplexer_3 (
    .in0(multiplexer_1_out), .in1(multiplexer_2_out), .out(multiplexer_3_out), .sel(rom_1_data_2[2]));
  Multiplexer #(.select(2), .width(8)) multiplexer_4 (
    .in0(multiplexer_3_out), .in1(adder_2_out), .in2(subtractor_2_out), .in3(bit_extender_1_out),
    .out(multiplexer_4_out), .sel(rom_1_data));
endmodule
